// Logisim project branch_control.circ as structural Verilog: 2 circuits, main circuit branch_control
module branch_control (
  input  [31:0] PC_in,
  input  jump,
  input  flag,
  input  [15:0] offset,
  output [31:0] PC_out
);

  wire jump_t;
  wire [31:0] multiplier_1_out, pc, sum;

  Multiplier #(.width(32)) multiplier_1 (
    .a({{16{1'b0}}, offset}), .b(32'h4), .out(multiplier_1_out));  // open: cin, cout
  Adder #(.width(32)) adder_1 (.a(PC_in), .b(32'h4), .out(pc));  // open: cin, cout
  Multiplexer #(.width(32), .enable("false")) multiplexer_1 (.in0(pc), .in1(sum), .out(PC_out), .sel(jump_t));
  and and_1 (jump_t, jump, flag);
  Adder #(.width(32)) adder_2 (.a(pc), .b(multiplier_1_out), .out(sum));  // open: cin, cout

  // Other names for the same wires on the sheet: hypothesis = flag; if = jump

  // Notes on the sheet:
  //   Direccion de la
  //   Instruccion Actual
  //   Instruccion de Salto
  //   Condicion de Salto
  //   Tamanno de Salto (k)
  //   tamanno de palabra
  //   Direccion de la
  //   Proxima Instruccion
endmodule

module test (
  input  [31:0] in_1,
  input  in_2,
  input  in_3,
  input  [15:0] in_4,
  output [31:0] out_5
);

  // Probe on in_1
  // Probe on in_4
  branch_control branch_control_1 (.PC_in(in_1), .jump(in_2), .flag(in_3), .offset(in_4), .PC_out(out_5));
  // Probe on out_5
endmodule
