// Logisim project cpu.circ as structural Verilog: 11 circuits, main circuit cpu
module cpu (
  input  clk,
  input  ram_end,
  input  clr,
  input  [31:0] ram_data,
  input  load_end,
  output [31:0] ram_read_addr,
  output cpu_end,
  output need_read,
  output halt,
  output tty_enable,
  output [6:0] tty_out,
  output [31:0] data
);

  wire beq, bgtz, blez, bltz, bneq, comparator_2_eq, comparator_3_eq, comparator_4_eq, comparator_5_eq,
       cpu_end_0, cpu_end_1, cpu_end_2, d_ff_1_q, d_ff_2_q, data_path_1_even, data_path_1_negative_flag,
       data_path_1_zero_flag, demultiplexer_2_out0, demultiplexer_2_out1, \end , eq, fin, fin_2, greater,
       hypothesis, immediate, is_comparission, is_copy, is_hilo, is_jump, is_random, J, JR, less, LW,
       multiplexer_12_out, multiplexer_15_out, not_1_out, not_2_out, not_3_out, on_memory, or_1_out,
       or_4_out, or_5_out, or_6_out, POP, rw, SHi, SLo, sw;
  wire [1:0] data_selector, dsel;
  wire [2:0] hyp_sel;
  wire [3:0] alu_selector;
  wire [4:0] DA, multiplexer_2_out, multiplexer_5_out, multiplexer_16_out, register_d, register_s, register_t;
  wire [5:0] func_code;
  wire [5:3] op_code;
  wire [15:0] multiplexer_1_out, offset;
  wire [25:0] jump;
  wire [31:0] adder_2_out, bit_extender_1_out, const2, constant, constant_2, constt2, fromRam, Hi, hi_t,
       instruction, Lo, lo_t, multiplexer_3_out, multiplexer_4_out, multiplexer_6_out, multiplexer_9_out,
       multiplexer_11_out, multiplexer_17_out, pc_current, pc_next, ram, rnd;
  wire [31:7] A;

  Multiplexer #(.width(16)) multiplexer_1 (
    .in0({16{1'b0}}), .in1(offset), .out(multiplexer_1_out), .sel(hypothesis));  // open: en
  not not_1 (not_1_out, halt);
  Multiplexer #(.width(5)) multiplexer_2 (
    .in0(register_d), .in1(register_t), .out(multiplexer_2_out), .sel(or_1_out));  // open: en
  or or_1 (or_1_out, immediate, LW);
  Multiplexer #(.width(32), .enable("false")) multiplexer_3 (
    .in0({32{1'b0}}), .in1(32'h1), .out(multiplexer_3_out), .sel(greater));
  Multiplexer #(.width(32), .enable("false")) multiplexer_4 (
    .in0({32{1'b0}}), .in1(32'h1), .out(multiplexer_4_out), .sel(greater));
  Comparator #(.width(6)) comparator_1 (.a({op_code, hyp_sel}), .b(6'b101011), .eq(sw));  // open: gt, lt
  or or_2 (need_read, POP, LW);
  Register #(.width(32)) PC (.D(pc_next), .en(fin), .Q(pc_current), .clk(clk), .clr(clr));
  and and_1 (\end , ram_end, not_1_out);
  Multiplexer #(.width(5), .enable("false")) multiplexer_5 (
    .in0(multiplexer_2_out), .in1({5{1'b1}}), .out(multiplexer_5_out), .sel(POP));
  Multiplexer #(.width(32)) multiplexer_6 (
    .in0(multiplexer_3_out), .in1(multiplexer_4_out), .out(multiplexer_6_out), .sel(immediate));  // open: en
  branch_control branch_control_1 (
    .PC_in(pc_current), .jump(is_jump), .flag(hypothesis), .offset(multiplexer_1_out), .PC_out(pc_next),
    .J(J), .JR(JR), .constant(jump), .R_s({A, tty_out}));
  D_Flip_Flop d_ff_1 (.clk(clk), .D(\end ), .Q(d_ff_1_q), .reset(clr));  // open: Qn, preset, en
  Demultiplexer #(.enable("false")) demultiplexer_1 (
    .out0(cpu_end_0), .out1(cpu_end_1), .in(d_ff_1_q), .sel(on_memory));
  Register #(.width(32)) register_1 (.D(ram_data), .en(not_2_out), .Q(instruction), .clk(clk), .clr(clr));
  not not_2 (not_2_out, on_memory);
  Multiplexer #(.width(32)) multiplexer_7 (
    .in0(constant), .in1(multiplexer_6_out), .out(const2), .sel(is_comparission));  // open: en
  Adder #(.width(32)) adder_1 (.a({A, tty_out}), .b(bit_extender_1_out), .out(fromRam));  // open: cin, cout
  assign bit_extender_1_out = {{16{offset[15]}}, offset};  // Bit_Extender bit_extender_1
  or or_3 (fin, cpu_end_0, fin_2);
  is_tty is_tty_1 (.opcode({op_code, hyp_sel}), .is_tty(tty_enable), .funcode(func_code), .CLK(clk), .END(fin));
  Multiplexer #(.width(5), .enable("false")) multiplexer_8 (
    .in0(multiplexer_5_out), .in1(register_d), .out(DA), .sel(is_random));
  or or_4 (or_4_out, LW, POP);
  instruction_decoder instruction_decoder_1 (
    .instruction(instruction), .op_code({op_code, hyp_sel}), .Rs(register_s), .Rt(register_t),
    .Rd(register_d), .func_code(func_code), .constant(constant), .jump(jump), .alu_selector(alu_selector),
    .immediate(immediate), .d_in_selector(dsel), .data_path_rw(rw), .halt(halt),
    .comparisiion(is_comparission), .is_jump(is_jump), .is_copy(is_copy), .is_on_memory(on_memory), .LW(LW),
    .POP(POP), .offset(offset));
  Comparator #(.width(6)) comparator_2 (.a(func_code), .b(6'b000010), .eq(comparator_2_eq));  // open: gt, lt
  Comparator #(.width(6)) comparator_3 (.a({op_code, hyp_sel}), .b({6{1'b1}}), .eq(comparator_3_eq));  // open: gt, lt
  Random #(.width(32)) u_rnd (.clk(clk), .out(rnd));  // open: next, clr
  Multiplexer #(.width(32), .enable("false")) multiplexer_9 (
    .in0(constt2), .in1(ram_data), .out(multiplexer_9_out), .sel(or_4_out));
  is_hilo is_hilo_1 (
    .a6(func_code[0]), .a5(func_code[1]), .a4(func_code[2]), .a3(func_code[3]), .a2(func_code[4]),
    .a1(func_code[5]), .s1(is_hilo));
  and and_2 (is_random, comparator_2_eq, comparator_3_eq);
  Multiplexer #(.width(2), .enable("false")) multiplexer_10 (
    .in0(dsel), .in1(2'b01), .out(data_selector), .sel(is_random));
  Adder #(.width(32)) adder_2 (.a(data), .b(32'h4), .out(adder_2_out));  // open: cin, cout
  Hi_Lo hi_lo_1 (
    .OP0(hyp_sel[0]), .OP1(hyp_sel[1]), .OP2(hyp_sel[2]), .OP3(op_code[3]), .OP4(op_code[4]),
    .OP5(op_code[5]), .F0(func_code[0]), .F1(func_code[1]), .F2(func_code[2]), .F3(func_code[3]),
    .F4(func_code[4]), .F5(func_code[5]), .SHi(SHi), .SLo(SLo));
  Multiplexer #(.width(32), .enable("false")) multiplexer_11 (
    .in0(multiplexer_9_out), .in1(adder_2_out), .out(multiplexer_11_out), .sel(POP));
  D_Flip_Flop d_ff_2 (.clk(clk), .D(or_5_out), .Q(d_ff_2_q), .reset(clr));  // open: Qn, preset, en
  or or_5 (or_5_out, demultiplexer_2_out0, cpu_end_1);
  Multiplexer #(.enable("false")) multiplexer_12 (.in0(rw), .in1(1'b1), .out(multiplexer_12_out), .sel(is_random));
  Multiplexer #(.select(2), .width(32)) multiplexer_13 (
    .in0(const2), .in1(Hi), .in2(Lo), .out(constt2), .sel({SLo, SHi}));  // open: in3, en
  Multiplexer #(.width(32), .enable("false")) multiplexer_14 (
    .in0(multiplexer_11_out), .in1(rnd), .out(constant_2), .sel(is_random));
  Demultiplexer #(.enable("false")) demultiplexer_2 (
    .out0(demultiplexer_2_out0), .out1(demultiplexer_2_out1), .in(d_ff_2_q), .sel(multiplexer_15_out));
  Multiplexer #(.enable("false")) multiplexer_15 (
    .in0(\end ), .in1(load_end), .out(multiplexer_15_out), .sel(need_read));
  Multiplexer #(.width(5), .enable("false")) multiplexer_16 (
    .in0(register_t), .in1({5{1'b1}}), .out(multiplexer_16_out), .sel(POP));
  Register #(.width(32)) u_Hi (.D(hi_t), .en(is_hilo), .Q(Hi), .clk(clk));  // open: clr
  Register #(.width(32)) u_Lo (.D(lo_t), .en(is_hilo), .Q(Lo), .clk(clk));  // open: clr
  Demultiplexer #(.enable("false")) demultiplexer_3 (
    .out0(fin_2), .in(demultiplexer_2_out1), .sel(need_read));  // open: out1
  data_path data_path_1 (
    .s_a(register_s), .s_b(multiplexer_16_out), .dest_addr(DA), .constant(constant), .Ram(ram),
    .zero_flag(data_path_1_zero_flag), .negative_flag(data_path_1_negative_flag), .is_immediate(immediate),
    .d_in_selector(data_selector), .rst(clr), .greater(greater), .alu_selector(alu_selector), .equal(eq),
    .less(less), .even(data_path_1_even), .rw(multiplexer_12_out), .enable(fin), .constant_2(constant_2),
    .A({A, tty_out}), .B(data), .lo(lo_t), .hi(hi_t));
  D_Flip_Flop d_ff_3 (.clk(clk), .D(fin_2), .Q(cpu_end_2), .en(clr));  // open: Qn, preset, reset
  Multiplexer #(.width(32), .enable("false")) multiplexer_17 (
    .in0(fromRam), .in1(data), .out(multiplexer_17_out), .sel(POP));
  Multiplexer multiplexer_18 (.in0(1'b0), .in1(1'b1), .out(beq), .sel(eq));  // open: en
  Multiplexer multiplexer_19 (.in0(1'b0), .in1(1'b1), .out(bneq), .sel(not_3_out));  // open: en
  not not_3 (not_3_out, eq);
  Multiplexer multiplexer_20 (.in0(1'b0), .in1(1'b1), .out(blez), .sel(or_6_out));  // open: en
  or or_6 (or_6_out, greater, eq);
  Multiplexer multiplexer_21 (.in0(1'b0), .in1(1'b1), .out(bgtz), .sel(less));  // open: en
  Multiplexer multiplexer_22 (.in0(1'b0), .in1(1'b1), .out(bltz), .sel(greater));  // open: en
  Multiplexer #(.width(32), .enable("false")) multiplexer_23 (
    .in0(pc_current), .in1(multiplexer_17_out), .out(ram_read_addr), .sel(on_memory));
  Comparator #(.width(6)) comparator_4 (.a({op_code, hyp_sel}), .b({6{1'b0}}), .eq(comparator_4_eq));  // open: gt, lt
  Comparator #(.width(6)) comparator_5 (.a(func_code), .b(6'b001000), .eq(comparator_5_eq));  // open: gt, lt
  Comparator #(.width(6)) comparator_6 (.a({op_code, hyp_sel}), .b(6'b000010), .eq(J));  // open: gt, lt
  or or_7 (cpu_end, cpu_end_0, cpu_end_2, cpu_end_1);
  Multiplexer #(.select(3), .disabled(0)) multiplexer_24 (
    .in0(1'b1), .in1(bltz), .in2(1'b1), .in3(1'b0), .in4(beq), .in5(bneq), .in6(blez), .in7(bgtz),
    .out(hypothesis), .sel(hyp_sel), .en(is_jump));
  and and_3 (JR, comparator_4_eq, comparator_5_eq);

  // Other names for the same wires on the sheet: A[6:0] = tty_out; B[31:0] = data; fin_1 = cpu_end_0; mem = cpu_end_1;
  //   op_code[2:0] = hyp_sel; RAMDATA[31:0] = ram_data; write_ram = need_read

  // Notes on the sheet:
  //   D.ADDRESS
  //   COMPARISSIONS
  //   MEMORY_INST
  //   SPECIAL
  //   COPY FROM Hi/Lo
  //   random is the only special who writes
  //   can finally read
  //   JUMPS
endmodule

module cpu_test (
);

  wire clock_1_out, \end , fake_ram_1_end;
  wire [31:0] addr, fake_ram_1_data;

  fake_ram fake_ram_1 (
    .cycles(4'b0011), .clk(clock_1_out), .db0(32'h1), .db1(32'h2), .db2(32'h3), .db3(32'h4), .ad(addr),
    .data(fake_ram_1_data), .\end (fake_ram_1_end), .cpu_end(\end ));  // open: real_addr, CLR
  // Probe on fake_ram_1_data
  Clock clock_1 (.out(clock_1_out));
  cpu cpu_1 (
    .ram_end(fake_ram_1_end), .ram_data(fake_ram_1_data), .ram_read_addr(addr), .clk(clock_1_out),
    .cpu_end(\end ));  // open: need_read, halt, clr, tty_enable, tty_out, data, load_end
  // Probe on addr
endmodule

module fake_ram (
  input  [3:0] cycles,
  input  clk,
  input  [31:0] db0,
  input  cpu_end,
  input  [31:0] db1,
  input  [31:0] db2,
  input  [31:0] db3,
  input  [31:0] ad,
  input  CLR,
  output [31:0] data,
  output \end ,
  output [15:0] real_addr
);

  wire or_1_out;
  wire [1:0] db_flag;
  wire [31:0] blocks;
  wire [31:2] divider_2_out;
  wire [31:16] arddr;

  Divider #(.width(32)) divider_1 (.a(ad), .b(32'h10), .out({arddr, real_addr}), .rem(blocks));  // open: upper
  Multiplexer #(.select(2), .width(32), .enable("false")) multiplexer_1 (
    .in0(db0), .in1(db1), .in2(db2), .in3(db3), .out(data), .sel(db_flag));
  Divider #(.width(32)) divider_2 (.a(blocks), .b(32'h4), .out({divider_2_out, db_flag}));  // open: upper, rem
  waita waita_1 (.cycles(cycles), .clk(clk), .cpu_end(or_1_out), .\end (\end ));
  or or_1 (or_1_out, cpu_end, CLR);

  // Other names for the same wires on the sheet: arddr[15:0] = real_addr; real_arddr[15:0] = real_addr
endmodule

module waita (
  input  clk,
  input  [3:0] cycles,
  input  cpu_end,
  output \end 
);

  wire not_1_out;
  wire [3:0] counter_1_q;

  Counter #(.width(4), .max('hf)) counter_1 (
    .count(not_1_out), .Q(counter_1_q), .clk(clk), .clr(cpu_end));  // open: load, D, carry
  not not_1 (not_1_out, \end );
  Comparator #(.width(4)) comparator_1 (.a(counter_1_q), .b(cycles), .eq(\end ));  // open: gt, lt
endmodule

module Hi_Lo (
  input  OP0,
  input  OP1,
  input  OP2,
  input  OP3,
  input  OP4,
  input  OP5,
  input  F0,
  input  F1,
  input  F2,
  input  F3,
  input  F4,
  input  F5,
  output SHi,
  output SLo
);

  wire not_1_out, not_2_out, not_3_out, not_4_out, not_5_out, not_6_out, not_7_out, not_8_out, not_9_out,
       not_10_out, not_11_out, not_12_out, not_13_out, not_14_out, not_15_out, not_16_out, not_17_out,
       not_18_out, not_19_out, not_20_out, not_21_out;

  not not_1 (not_1_out, OP0);
  not not_2 (not_2_out, OP1);
  not not_3 (not_3_out, OP2);
  not not_4 (not_4_out, OP3);
  not not_5 (not_5_out, OP4);
  not not_6 (not_6_out, OP5);
  not not_7 (not_7_out, F0);
  not not_8 (not_8_out, F1);
  not not_9 (not_9_out, F2);
  not not_10 (not_10_out, F3);
  not not_11 (not_11_out, F5);
  not not_12 (not_12_out, OP0);
  not not_13 (not_13_out, OP1);
  not not_14 (not_14_out, OP2);
  not not_15 (not_15_out, OP3);
  not not_16 (not_16_out, OP4);
  not not_17 (not_17_out, OP5);
  not not_18 (not_18_out, F0);
  not not_19 (not_19_out, F2);
  not not_20 (not_20_out, F3);
  not not_21 (not_21_out, F5);
  and and_1 (SHi, not_1_out, not_2_out, not_3_out, not_4_out, not_5_out, not_6_out, not_7_out, not_8_out, not_9_out, not_10_out, F4, not_11_out);
  and and_2 (SLo, not_12_out, not_13_out, not_14_out, not_15_out, not_16_out, not_17_out, not_18_out, F1, not_19_out, not_20_out, F4, not_21_out);
endmodule

module is_tty (
  input  [5:0] opcode,
  input  [5:0] funcode,
  input  CLK,
  input  END,
  output is_tty
);

  wire all_true_1_s1, and_1_out, and_2_out, and_3_out, MAX, one_1_s1;

  all_true all_true_1 (
    .i1(opcode[0]), .i2(opcode[1]), .i3(opcode[2]), .i4(opcode[3]), .i5(opcode[4]), .i6(opcode[5]),
    .s1(all_true_1_s1));
  one one_1 (
    .i1(funcode[0]), .i2(funcode[1]), .i3(funcode[2]), .i4(funcode[3]), .i5(funcode[4]), .i6(funcode[5]),
    .s1(one_1_s1));
  and and_1 (and_1_out, all_true_1_s1, one_1_s1);
  and and_2 (and_2_out, and_1_out, ~MAX);  // AND_Gate
  Counter #(.width(1), .max('h1)) counter_1 (.count(and_2_out), .carry(MAX), .clk(CLK), .clr(END));  // open: load, D, Q
  and and_3 (and_3_out, and_1_out, ~MAX);  // AND_Gate
  and and_4 (is_tty, END, and_3_out);
endmodule

module all_true (
  input  i1,
  input  i2,
  input  i3,
  input  i4,
  input  i5,
  input  i6,
  output s1
);

  and and_1 (s1, i1, i2, i3, i4, i5, i6);
endmodule

module one (
  input  i1,
  input  i2,
  input  i3,
  input  i4,
  input  i5,
  input  i6,
  output s1
);

  wire not_1_out, not_2_out, not_3_out, not_4_out, not_5_out;

  not not_1 (not_1_out, i2);
  not not_2 (not_2_out, i3);
  not not_3 (not_3_out, i4);
  not not_4 (not_4_out, i5);
  not not_5 (not_5_out, i6);
  and and_1 (s1, i1, not_1_out, not_2_out, not_3_out, not_4_out, not_5_out);
endmodule

module is_hilo (
  input  a6,
  input  a5,
  input  a4,
  input  a3,
  input  a2,
  input  a1,
  output s1
);

  wire not_1_out, not_2_out;

  not not_1 (not_1_out, a1);
  not not_2 (not_2_out, a4);
  and and_1 (s1, not_1_out, a2, a3, not_2_out);
endmodule

module load_ram (
  input  [3:0] cycles,
  input  clk,
  input  reset,
  input  [31:0] data,
  input  [31:0] ad,
  input  RW,
  input  CLR,
  output \end ,
  output [15:0] real_addr,
  output [31:0] db0,
  output [31:0] db1,
  output [31:0] db2,
  output [31:0] db3,
  output [3:0] mask
);

  wire or_1_out;
  wire [1:0] db_flag;
  wire [31:0] blocks;
  wire [31:2] divider_2_out;
  wire [31:16] arddr;

  Divider #(.width(32)) divider_1 (.a(ad), .b(32'h10), .out({arddr, real_addr}), .rem(blocks));  // open: upper
  Multiplexer #(.select(2), .width(32), .enable("false")) multiplexer_1 (
    .in0(db0), .in1(db1), .in2(db2), .in3(db3), .out(data), .sel(db_flag));
  Divider #(.width(32)) divider_2 (.a(blocks), .b(32'h4), .out({divider_2_out, db_flag}));  // open: upper, rem
  waita waita_1 (.cycles(cycles), .clk(clk), .cpu_end(or_1_out), .\end (\end ));
  or or_1 (or_1_out, reset, CLR);
  Decoder #(.select(2), .enable("false")) decoder_1 (
    .out0(mask[0]), .out1(mask[1]), .out2(mask[2]), .out3(mask[3]), .sel(db_flag));

  // Other names for the same wires on the sheet: arddr[15:0] = real_addr; real_arddr[15:0] = real_addr
endmodule

module memory_address (
  input  [31:0] ALU,
  input  [31:0] PC,
  input  [31:0] SP,
  input  POP,
  input  PUSH,
  input  LW,
  input  SW,
  input  PC_ADDRESS,
  output [31:0] MEMORY
);

  wire [1:0] or_2_out;
  wire [31:0] multiplexer_1_out, subtractor_1_out;

  Subtractor #(.width(32)) subtractor_1 (.a(SP), .b(32'h4), .out(subtractor_1_out));  // open: bin, bout
  Multiplexer #(.width(32), .enable("false")) multiplexer_1 (
    .in0(SP), .in1(subtractor_1_out), .out(multiplexer_1_out), .sel(PUSH));
  or or_1 (or_2_out[1], PUSH, POP, PC_ADDRESS);
  Multiplexer #(.select(2), .width(32), .enable("false")) multiplexer_2 (
    .in0(PC), .in1(ALU), .in2(multiplexer_1_out), .in3(PC), .out(MEMORY), .sel(or_2_out));
  or or_2 (or_2_out[0], PC_ADDRESS, LW, SW);
endmodule
