// Logisim project data_path.circ as structural Verilog
module ALU (
  input  [31:0] A,
  input  [31:0] B,
  input  [3:0] S,
  output [31:0] R,
  output Zero,
  output Neg,
  output Even,
  output Less,
  output Equal,
  output Greater,
  output [31:0] lo,
  output [31:0] hi
);

  wire greater_s, greater_u, less_s, less_u, sign_mul, sltu;
  wire [14:0] sm_h;
  wire [15:0] sm_l;
  wire [15:15] um_h;
  wire [31:0] add, \and , \nor , \or , s_rem, sdiv, sleft, sright, sub, \xor ;
  wire [31:31] udiv;

  Multiplexer #(.enable("false")) multiplexer_1 (.in0(less_s), .in1(less_u), .out(Less), .sel(sltu));
  Multiplexer #(.enable("false")) multiplexer_2 (.in0(greater_s), .in1(greater_u), .out(Greater), .sel(sltu));
  Comparator #(.width(4)) comparator_1 (.a(4'b0011), .b(S), .eq(sltu));  // open: gt, lt
  Comparator #(.width(32)) comparator_2 (.a(A), .b(B), .gt(less_s), .eq(Equal), .lt(greater_s));
  Comparator #(.width(32)) comparator_3 (.a(R), .b({32{1'b0}}), .eq(Zero), .lt(Neg));  // open: gt
  not not_1 (Even, R[0]);
  Comparator #(.width(32), .mode("unsigned")) comparator_4 (.a(A), .b(B), .gt(less_u), .lt(greater_u));  // open: eq
  Adder #(.width(32)) adder_1 (.a(A), .b(B), .out(add));  // open: cin, cout
  Subtractor #(.width(32)) subtractor_1 (.a(A), .b(B), .out(sub));  // open: bin, bout
  Multiplier #(.width(32)) multiplier_1 (.a(A), .b(B), .out({um_h[15], sm_h, sm_l}));  // open: cin, cout
  Divider #(.width(32)) divider_1 (.a(A), .b(B), .out({udiv[31], sdiv[30:0]}), .rem(s_rem));  // open: upper
  assign \and  = A & B;  // AND_Gate and_1, 32 bits wide
  assign \or  = A | B;  // OR_Gate or_1, 32 bits wide
  assign \nor  = ~(A | B);  // NOR_Gate nor_1, 32 bits wide
  assign \xor  = A ^ B;  // XOR_Gate xor_1, 32 bits wide
  Multiplier #(.width(1)) multiplier_2 (.a(A[31]), .b(B[31]), .out(sign_mul));  // open: cin, cout
  Divider #(.width(1)) divider_2 (.a(A[31]), .b(B[31]), .out(sdiv[31]));  // open: upper, rem
  Multiplexer #(.select(4), .width(32), .enable("false")) multiplexer_3 (
    .in0(add), .in1(sub), .in2({um_h[15], sm_h, sm_l}), .in3({udiv[31], sdiv[30:0]}), .in4(\and ),
    .in5(\or ), .in6(sleft), .in7(sright), .in8(sdiv), .in9({sdiv[31], sm_h, sm_l}), .in10(\nor ),
    .in11(\xor ), .out(R), .sel(S));  // open: in12, in13, in14, in15
  Multiplexer #(.select(4), .width(32), .enable("false")) multiplexer_4 (
    .in2({{16{1'b0}}, sm_l}), .in3({udiv[31], sdiv[30:0]}), .in8(sdiv), .in9({{16{1'b0}}, sm_l}), .out(lo),
    .sel(S));  // open: in0, in1, in4, in5, in6, in7, in10, in11, in12, in13, in14, in15
  Shifter #(.width(32)) shifter_1 (.in(A), .\dist ({5{1'b1}}), .out(sleft));
  Shifter #(.width(32), .shift("lr")) shifter_2 (.in(A), .\dist ({5{1'b1}}), .out(sright));
  Multiplexer #(.select(4), .width(32), .enable("false")) multiplexer_5 (
    .in2({{16{1'b0}}, um_h[15], sm_h}), .in3(s_rem), .in8(s_rem), .in9({{16{1'b0}}, sdiv[31], sm_h}),
    .out(hi), .sel(S));  // open: in0, in1, in4, in5, in6, in7, in10, in11, in12, in13, in14, in15

  // Other names for the same wires on the sheet: sign_a = A[31]; sign_b = B[31]; h[31:0] = hi; l[31:0] = lo;
  //   res[31:0] = R; udiv[30:0] = sdiv[30:0]; selector[3:0] = S; smult[31:0] = {sdiv[31], sm_h, sm_l};
  //   um_h[14:0] = sm_h; umul[31:0] = {um_h[15], sm_h, sm_l}; sign_div = sdiv[31]; sm_h[15] = sdiv[31];
  //   um_l[15:0] = sm_l
endmodule

module register_file (
  input  [4:0] DA,
  input  [31:0] DI,
  input  R_W,
  input  [4:0] SA,
  input  [4:0] SB,
  input  Clk,
  input  Reset,
  output [31:0] A,
  output [31:0] B
);

  wire w1, w2, w3, w4, w5, w6, w7, w8, w9, w10, w11, w12, w13, w14, w15, w16, w17, w18, w19, w20, w21, w22,
       w23, w24, w25, w26, w27, w28, w29, w30, w31, w32;
  wire [31:0] r1, r2, r3, r4, r5, r6, r7, r8, r9, r10, r11, r12, r13, r14, r15, r16, r17, r18, r19, r20, r21,
       r22, r23, r24, r25, r26, r27, r28, r29, r30, r31, r32;

  Multiplexer #(.select(5), .width(32), .enable("false")) multiplexer_1 (
    .in0(r1), .in1(r2), .in2(r3), .in3(r4), .in4(r5), .in5(r6), .in6(r7), .in7(r8), .in8(r9), .in9(r10),
    .in10(r11), .in11(r12), .in12(r13), .in13(r14), .in14(r15), .in15(r16), .in16(r17), .in17(r18),
    .in18(r19), .in19(r20), .in20(r21), .in21(r22), .in22(r23), .in23(r24), .in24(r25), .in25(r26),
    .in26(r27), .in27(r28), .in28(r29), .in29(r30), .in30(r31), .in31(r32), .out(A), .sel(SA));
  Register #(.width(32)) register_1 (.D(DI), .en(w1), .Q(r1), .clk(Clk), .clr(Reset));
  Register #(.width(32)) register_2 (.D(DI), .en(w2), .Q(r2), .clk(Clk), .clr(Reset));
  Register #(.width(32)) register_3 (.D(DI), .en(w3), .Q(r3), .clk(Clk), .clr(Reset));
  Register #(.width(32)) register_4 (.D(DI), .en(w4), .Q(r4), .clk(Clk), .clr(Reset));
  Register #(.width(32)) register_5 (.D(DI), .en(w5), .Q(r5), .clk(Clk), .clr(Reset));
  Register #(.width(32)) register_6 (.D(DI), .en(w6), .Q(r6), .clk(Clk), .clr(Reset));
  // Probe on A
  Multiplexer #(.select(5), .width(32), .enable("false")) multiplexer_2 (
    .in0(r1), .in1(r2), .in2(r3), .in3(r4), .in4(r5), .in5(r6), .in6(r7), .in7(r8), .in8(r9), .in9(r10),
    .in10(r11), .in11(r12), .in12(r13), .in13(r14), .in14(r15), .in15(r16), .in16(r17), .in17(r18),
    .in18(r19), .in19(r20), .in20(r21), .in21(r22), .in22(r23), .in23(r24), .in24(r25), .in25(r26),
    .in26(r27), .in27(r28), .in28(r29), .in29(r30), .in30(r31), .in31(r32), .out(B), .sel(SB));
  Register #(.width(32)) register_7 (.D(DI), .en(w7), .Q(r7), .clk(Clk), .clr(Reset));
  Register #(.width(32)) register_8 (.D(DI), .en(w8), .Q(r8), .clk(Clk), .clr(Reset));
  Register #(.width(32)) register_9 (.D(DI), .en(w9), .Q(r9), .clk(Clk), .clr(Reset));
  Register #(.width(32)) register_10 (.D(DI), .en(w10), .Q(r10), .clk(Clk), .clr(Reset));
  Register #(.width(32)) register_11 (.D(DI), .en(w11), .Q(r11), .clk(Clk), .clr(Reset));
  Register #(.width(32)) register_12 (.D(DI), .en(w12), .Q(r12), .clk(Clk), .clr(Reset));
  // Probe on B
  Register #(.width(32)) register_13 (.D(DI), .en(w13), .Q(r13), .clk(Clk), .clr(Reset));
  Register #(.width(32)) register_14 (.D(DI), .en(w14), .Q(r14), .clk(Clk), .clr(Reset));
  Register #(.width(32)) register_15 (.D(DI), .en(w15), .Q(r15), .clk(Clk), .clr(Reset));
  Register #(.width(32)) register_16 (.D(DI), .en(w16), .Q(r16), .clk(Clk), .clr(Reset));
  Register #(.width(32)) register_17 (.D(DI), .en(w17), .Q(r17), .clk(Clk), .clr(Reset));
  Register #(.width(32)) register_18 (.D(DI), .en(w18), .Q(r18), .clk(Clk), .clr(Reset));
  Demultiplexer #(.select(5), .disabled(0)) demultiplexer_1 (
    .out0(w1), .out1(w2), .out2(w3), .out3(w4), .out4(w5), .out5(w6), .out6(w7), .out7(w8), .out8(w9),
    .out9(w10), .out10(w11), .out11(w12), .out12(w13), .out13(w14), .out14(w15), .out15(w16), .out16(w17),
    .out17(w18), .out18(w19), .out19(w20), .out20(w21), .out21(w22), .out22(w23), .out23(w24), .out24(w25),
    .out25(w26), .out26(w27), .out27(w28), .out28(w29), .out29(w30), .out30(w31), .out31(w32), .in(1'b1),
    .sel(DA), .en(R_W));
  Register #(.width(32)) register_19 (.D(DI), .en(w19), .Q(r19), .clk(Clk), .clr(Reset));
  Register #(.width(32)) register_20 (.D(DI), .en(w20), .Q(r20), .clk(Clk), .clr(Reset));
  Register #(.width(32)) register_21 (.D(DI), .en(w21), .Q(r21), .clk(Clk), .clr(Reset));
  Register #(.width(32)) register_22 (.D(DI), .en(w22), .Q(r22), .clk(Clk), .clr(Reset));
  Register #(.width(32)) register_23 (.D(DI), .en(w23), .Q(r23), .clk(Clk), .clr(Reset));
  Register #(.width(32)) register_24 (.D(DI), .en(w24), .Q(r24), .clk(Clk), .clr(Reset));
  Register #(.width(32)) register_25 (.D(DI), .en(w25), .Q(r25), .clk(Clk), .clr(Reset));
  Register #(.width(32)) register_26 (.D(DI), .en(w26), .Q(r26), .clk(Clk), .clr(Reset));
  Register #(.width(32)) register_27 (.D(DI), .en(w27), .Q(r27), .clk(Clk), .clr(Reset));
  Register #(.width(32)) register_28 (.D(DI), .en(w28), .Q(r28), .clk(Clk), .clr(Reset));
  Register #(.width(32)) register_29 (.D(DI), .en(w29), .Q(r29), .clk(Clk), .clr(Reset));
  Register #(.width(32)) register_30 (.D(DI), .en(w30), .Q(r30), .clk(Clk), .clr(Reset));
  Register #(.width(32)) register_31 (.D(DI), .en(w31), .Q(r31), .clk(Clk), .clr(Reset));
  Register #(.width(32)) register_32 (.D(DI), .en(w32), .Q(r32), .clk(Clk), .clr(Reset));

  // Other names for the same wires on the sheet: rst = Reset; w = R_W

  // Notes on the sheet:
  //   Inputs
  //   Data Address
  //   Data In
  //   Read/Write
  //   Selector A
  //   Selector B
  //   pincha con el 1 porque r/w es el enable
  //   Outputs
  //   Data A
  //   Data B
endmodule

module data_path (
  input  [4:0] s_a,
  input  [4:0] s_b,
  input  [4:0] dest_addr,
  input  [3:0] alu_selector,
  input  rst,
  input  [31:0] constant_2,
  input  [31:0] constant,
  input  [1:0] d_in_selector,
  input  [31:0] Ram,
  input  is_immediate,
  input  rw,
  input  enable,
  output [31:0] A,
  output zero_flag,
  output negative_flag,
  output [31:0] B,
  output even,
  output greater,
  output less,
  output equal,
  output [31:0] lo,
  output [31:0] hi
);

  wire clock_1_out, rw_t;
  wire [31:0] ALU, B_t, d_in;

  Multiplexer #(.width(32), .enable("false")) multiplexer_1 (.in0(B), .in1(constant), .out(B_t), .sel(is_immediate));
  and and_1 (rw_t, rw, enable);
  Multiplexer #(.select(2), .width(32), .enable("false")) multiplexer_2 (
    .in0(ALU), .in1(constant_2), .in2(A), .in3(Ram), .out(d_in), .sel(d_in_selector));
  register_file register_file_1 (
    .DA(dest_addr), .DI(d_in), .R_W(rw_t), .SA(s_a), .SB(s_b), .Clk(clock_1_out), .Reset(rst), .A(A), .B(B));
  Clock clock_1 (.out(clock_1_out));
  // Probe on A
  // Probe on B
  // Probe on ALU
  ALU alu_1 (
    .A(A), .B(B_t), .S(alu_selector), .R(ALU), .Zero(zero_flag), .Neg(negative_flag), .Even(even),
    .Less(less), .Equal(equal), .Greater(greater), .lo(lo), .hi(hi));

  // Other names for the same wires on the sheet: k[31:0] = constant; k2[31:0] = constant_2

  // Notes on the sheet:
  //   enable to avoid executing an instruction multiple times while we wait for RAM
endmodule
