// Logisim project instruction_decoder.circ as structural Verilog: 5 circuits, main circuit instruction_decoder
module instruction_decoder (
  input  [31:0] instruction,
  output [5:0] op_code,
  output [4:0] Rs,
  output [4:0] Rt,
  output [4:0] Rd,
  output [5:0] func_code,
  output [31:0] constant,
  output [25:0] jump,
  output [3:0] alu_selector,
  output immediate,
  output [1:0] d_in_selector,
  output data_path_rw,
  output halt
);

  wire comparator_1_eq, comparator_2_eq, not_1_out, not_2_out;
  wire [3:0] alu_s_imm, alu_s_reg;

  alu_selector_translator alu_selector_translator_1 (
    .a(instruction[0]), .b(instruction[1]), .c(instruction[2]), .d(instruction[3]), .e(instruction[4]),
    .f(instruction[5]), .s1(alu_s_reg[0]), .s2(alu_s_reg[1]), .s3(alu_s_reg[2]), .s4(alu_s_reg[3]));
  not not_1 (not_1_out, instruction[30]);
  and and_1 (immediate, instruction[29], not_1_out, not_2_out);
  not not_2 (not_2_out, instruction[31]);
  immediate_translator immediate_translator_1 (
    .a1(instruction[26]), .a2(instruction[27]), .a3(instruction[28]), .s1(alu_s_imm[0]), .s2(alu_s_imm[1]),
    .s3(alu_s_imm[2]), .s4(alu_s_imm[3]));
  Comparator #(.width(6)) comparator_1 (.a({6{1'b1}}), .b(instruction[5:0]), .eq(comparator_1_eq));  // open: gt, lt
  Multiplexer #(.width(4), .enable("false")) multiplexer_1 (
    .in0(alu_s_reg), .in1(alu_s_imm), .out(alu_selector), .sel(immediate));
  Comparator #(.width(6)) comparator_2 (
    .a(instruction[31:26]), .b(instruction[5:0]), .eq(comparator_2_eq));  // open: gt, lt
  and and_2 (halt, comparator_2_eq, comparator_1_eq);

  assign constant = {{16{1'b0}}, instruction[15:0]};
  assign d_in_selector = 2'b00;
  assign data_path_rw = 1'b1;
  assign func_code = instruction[5:0];
  assign jump = {instruction[20:16], instruction[20:0]};
  assign op_code = instruction[31:26];
  assign Rd = instruction[15:11];
  assign Rs = instruction[25:21];
  assign Rt = instruction[20:16];

  // Other names for the same wires on the sheet: register_s[4:0] = instruction[25:21];
  //   constant_t[15:0] = instruction[15:0]; full_constant[15:0] = instruction[15:0]; x[4:0] = instruction[10:6];
  //   register_d[4:0] = instruction[15:11]; register_t[4:0] = instruction[20:16]

  // Notes on the sheet:
  //   001 <=> immediate
  //   000 <=> no wait
endmodule

module alu_selector_translator (
  input  a,
  input  b,
  input  c,
  input  d,
  input  e,
  input  f,
  output s1,
  output s2,
  output s3,
  output s4
);

  wire and_1_out, and_2_out, and_4_out, and_5_out, and_6_out, and_7_out, and_8_out, and_9_out, and_10_out,
       not_1_out, not_2_out, not_3_out, not_4_out, not_5_out, not_6_out, not_7_out, not_8_out, not_9_out,
       not_10_out, not_11_out;

  not not_1 (not_1_out, f);
  not not_2 (not_2_out, e);
  not not_3 (not_3_out, d);
  not not_4 (not_4_out, b);
  not not_5 (not_5_out, b);
  not not_6 (not_6_out, e);
  not not_7 (not_7_out, b);
  not not_8 (not_8_out, d);
  not not_9 (not_9_out, d);
  not not_10 (not_10_out, e);
  not not_11 (not_11_out, f);
  and and_1 (and_1_out, d, e);
  and and_2 (and_2_out, c, not_1_out);
  and and_3 (s2, d, not_2_out);
  and and_4 (and_4_out, not_3_out, f);
  and and_5 (and_5_out, d, e);
  and and_6 (and_6_out, not_4_out, c);
  and and_7 (and_7_out, not_5_out, not_6_out, f);
  and and_8 (and_8_out, not_7_out, not_8_out, e);
  and and_9 (and_9_out, not_9_out, e, f);
  and and_10 (and_10_out, c, not_10_out, not_11_out);
  or or_1 (s1, and_1_out, and_2_out);
  or or_2 (s3, and_4_out, and_5_out, and_6_out);
  or or_3 (s4, and_7_out, and_8_out, and_9_out, and_10_out);
endmodule

module d_in_selector (
  input  immediate,
  output s1,
  output s2
);


  assign s1 = immediate;
  assign s2 = 1'b0;
endmodule

module immediate_translator (
  input  a1,
  input  a2,
  input  a3,
  output s1,
  output s2,
  output s3,
  output s4
);

  wire not_1_out;

  not not_1 (not_1_out, a2);
  or or_1 (s4, a3, a2);
  and and_1 (s2, a1, not_1_out);

  assign s1 = a2;
  assign s3 = a2;
endmodule

module test_instruction (
);

  wire data_path_1_p10, data_path_1_p11, data_path_1_p12, data_path_1_p13, data_path_1_p14, data_path_1_p15,
       immediate, rw;
  wire [1:0] data_selector;
  wire [3:0] alu_selector;
  wire [4:0] register_d, register_s, register_t, x;
  wire [5:0] func_code, op_code;
  wire [25:0] jump;
  wire [31:0] constant, ram;

  // Probe on {6{1'b0}}
  // Probe on 6'b001000
  // Probe on 32'h20620020
  instruction_decoder instruction_decoder_1 (
    .instruction(32'h20620020), .op_code(op_code), .Rs(register_s), .Rt(register_t), .Rd(register_d),
    .func_code(func_code), .constant(constant), .jump(jump), .alu_selector(alu_selector),
    .immediate(immediate), .d_in_selector(data_selector), .data_path_rw(rw));  // open: halt
  // Probe on register_d
  // Probe on register_t
  // Probe on register_s
  // Probe on op_code
  // Probe on func_code
  // Probe on x
  // data_path data_path_1: pin names not known; wires that end beside it: register_t, register_d, register_s, rw, constant, ram, alu_selector, data_selector, immediate, data_path_1_p10, data_path_1_p11, data_path_1_p12, data_path_1_p13, data_path_1_p14, data_path_1_p15
  // Probe on constant

  // Notes on the sheet:
  //   instructions
  //   constant
  //   registers
  //   register
  //   instant
  //   idem
endmodule
